# Fritzing sketch ESP8266_HVAC_REV2 (saved by Fritzing 0.9.3b)
breadboards: 1

parts:
  U1 = NodeMCU V1.0
  DTH22_c\_Placa = Humidity and Temperature Sensor RHT03
  R1 = Photocell (LDR) [package=THT]
  R2 = Resistor [tolerance=±5% resistance=10k package=THT]
  LED1 = LED - 5mm [color="Red (633nm)" package="5 mm [THT]"]
  IR1 = TSOP312.., 314.. [package=THT]
  Q1 = TRANSISTOR_NPN [package=to-92]
  J1 = female pin header, 1 pin [form="♀ (female)"]
  J2 = male pin header, 1 pin [form="♂ (male)"]
  PIR = TSOP312.., 314.. [package=THT]
  J3 = female alternating pin header, 3 pins [form="♀ (female)"]
  J4 = male pin header, 3 pins [form="♂ (male)"]
  U2 = 2.5mm Audio Jack [package=stereojack2.5mm_smd]  # not connected

nets:
  N1: U1.D1, J1.pin1
  N2: U1.D2, Q1.B
  3.3V: U1.3V3, DTH22_c\_Placa.Vcc, R2.Pin_0, LED1.anode, IR1.Vs
  N3: U1.D5, IR1.Data
  N4: U1.D6, J3.pin2
  N5: U1.Vin, J3.pin1
  GND: U1.GND, DTH22_c\_Placa.GND_2, R1.pin_0, IR1.GND, Q1.E, J3.pin3
  N6: U1.A0, R1.pin_1, R2.Pin_1
  N7: DTH22_c\_Placa.Data-signal, J2.pin1
  N8: LED1.cathode, Q1.C
  N9: PIR.GND, J4.pin1
  N10: PIR.Vs, J4.pin3
  N11: PIR.Data, J4.pin2

notes:
  - Amarelo
  + Vermelho
  Out Branco
  - azul
  + rojo
  Out cinzento

custom parts:
  NodeMCU V1.0: ESP8266 based NodeMCU
